# Fritzing sketch Final ISU (saved by Fritzing 0.9.3b)
breadboards: 1
perfboards: 2

parts:
  Part1 = Arduino Mega ADK (Rev3)
  7_Segment1 = 7 Segment Display
  7_Segment2 = 7 Segment Display
  7_Segment3 = 7 Segment Display
  7_Segment4 = 7 Segment Display
  7_Segment5 = 7 Segment Display
  7_Segment6 = 7 Segment Display
  S1 = Pushbutton [package="[THT]"]
  S2 = Pushbutton [package="[THT]"]
  S3 = Pushbutton [package="[THT]"]
  R1 = Resistor [tolerance=±5% resistance=1k package=THT]
  R2 = Resistor [tolerance=±5% resistance=1k package=THT]
  R3 = Resistor [tolerance=±5% resistance=1k package=THT]
  J1 = Piezo Speaker
  R4 = Resistor [tolerance=±5% resistance=220 package=THT]
  R5 = Resistor [tolerance=±5% resistance=220 package=THT]
  R6 = Resistor [tolerance=±5% resistance=220 package=THT]
  R7 = Resistor [tolerance=±5% resistance=220 package=THT]
  R8 = Resistor [tolerance=±5% resistance=220 package=THT]
  R9 = Resistor [tolerance=±5% resistance=220 package=THT]
  R10 = Resistor [tolerance=±5% resistance=1k package=THT]
  S5 = Toggle Switch [package=THT]
  R11 = Resistor [tolerance=±5% resistance=1k package=THT]
  LED1 = DUO LED RG [package="5 mm [THT]"]

nets:
  N1: Part1.A8, LED1.red_anode
  N2: Part1.A9, LED1.green_anode
  N3: Part1.A1, S3.Pin_3, S3.Pin_4, R3.Pin_1
  N4: Part1.A2, S2.Pin_3, S2.Pin_4, R2.Pin_1
  N5: Part1.A3, S1.Pin_3, S1.Pin_4, R1.Pin_1
  N6: Part1.A4, R10.Pin_1, S5.L2
  N7: Part1.GND, S1.Pin_1, S1.Pin_2, S2.Pin_1, S2.Pin_2, S3.Pin_1, S3.Pin_2, J1.pin1, R4.Pin_0, R5.Pin_0, R6.Pin_0, R7.Pin_0, R8.Pin_0, R9.Pin_0, S5.COM, R11.Pin_0
  N8: Part1.D12_PWM, J1.pin2
  N9: Part1.5V, 7_Segment2.Segment_DP, 7_Segment3.Segment_DP, 7_Segment4.Segment_DP, 7_Segment5.Segment_DP, R1.Pin_0, R2.Pin_0, R3.Pin_0, R10.Pin_0
  N10: Part1.D22, 7_Segment1.Segment_G
  N11: Part1.D23, 7_Segment1.Segment_F
  N12: Part1.D24, 7_Segment1.Segment_A
  N13: Part1.D25, 7_Segment1.Segment_B
  N14: Part1.D44, 7_Segment1.Segment_E
  N15: Part1.D45, 7_Segment1.Segment_D
  N16: Part1.D46, 7_Segment1.Segment_C
  N17: 7_Segment1.common_anode, R4.Pin_1
  N18: 7_Segment2.common_anode, R5.Pin_1
  N19: 7_Segment3.common_anode, R6.Pin_1
  N20: 7_Segment4.common_anode, R7.Pin_1
  N21: 7_Segment5.common_anode, R8.Pin_1
  N22: 7_Segment6.common_anode, R9.Pin_1
  N23: R11.Pin_1, LED1.common_cathode

notes:
  22 23 24 25 26 27 28 29 52 51 50 33 34 35 36 7 6 5 40 41 42 43
  ↓ ↓ ↓ ↓ ↓ ↓ ↓ ↓ ↓ ↓ ↓ ↓ ↓ ↓ ↓ ↓ ↓ ↓ ↓ ↓ ↓ ↓
  ↑ ↑ ↑ ↑ ↑ ↑ ↑ ↑ ↑ ↑ ↑ ↑ ↑ ↑ ↑ ↑ ↑ ↑ ↑ ↑
  44 45 46 47 48 49 32 31 30 53 2 3 4 39 38 37 8 9 10 11
